# Fritzing sketch s-11 (saved by Fritzing 0.9.2b)
breadboards: 1

parts:
  PSoC_Prototyping_kit1 = PSoC Prototyping kit [chip_label="PSoC Prototyping kit" package="DIP (Dual Inline) [THT]"]
  S1 = Pushbutton [package="[THT]"]
  LED1 = smd LED [color="Red (633nm)" package="0603 [SMD]"]
  R1 = Resistor [tolerance=±5% resistance=220 package="0603 [SMD]"]

nets:
  N1: PSoC_Prototyping_kit1.GND#0, LED1.cathode
  N2: PSoC_Prototyping_kit1.0.7, S1.Pin_1, S1.Pin_2
  N3: PSoC_Prototyping_kit1.1.6, R1.Pin_1
  N4: PSoC_Prototyping_kit1.GND#44, S1.Pin_3, S1.Pin_4
  N5: LED1.anode, R1.Pin_0

custom parts:
  PSoC Prototyping kit: A DIP stand-in part for whatever IC you want. With 46 pins on a 300mil dual inline package (DIP) footprint.
