# Fritzing sketch s-11 (saved by Fritzing 0.9.2b)
breadboards: 2

parts:
  S1 = Pushbutton [package="[THT]"]
  LED1 = smd LED [color="Red (633nm)" package="0603 [SMD]"]
  R1 = Resistor [tolerance=±5% resistance=220 package="0603 [SMD]"]
  LED2 = smd LED [color="Red (633nm)" package="0603 [SMD]"]
  R2 = Resistor [tolerance=±5% resistance=220 package="0603 [SMD]"]
  LED3 = smd LED [color="Red (633nm)" package="0603 [SMD]"]
  R3 = Resistor [tolerance=±5% resistance=220 package="0603 [SMD]"]
  PSoC_Prototyping_kit1 = PSoC Prototyping kit [chip_label="PSoC Prototyping kit" package="DIP (Dual Inline) [THT]"]

nets:
  N1: S1.Pin_1, S1.Pin_2, PSoC_Prototyping_kit1.0.7
  N2: S1.Pin_3, S1.Pin_4, PSoC_Prototyping_kit1.GND#44
  N3: LED1.cathode, LED2.cathode, LED3.cathode, PSoC_Prototyping_kit1.GND#0
  N4: LED1.anode, R1.Pin_0
  N5: R1.Pin_1, PSoC_Prototyping_kit1.1.4
  N6: LED2.anode, R2.Pin_0
  N7: R2.Pin_1, PSoC_Prototyping_kit1.1.5
  N8: LED3.anode, R3.Pin_0
  N9: R3.Pin_1, PSoC_Prototyping_kit1.1.6

custom parts:
  PSoC Prototyping kit: A DIP stand-in part for whatever IC you want. With 46 pins on a 300mil dual inline package (DIP) footprint.
